# Fritzing sketch PotLEDControlColor (saved by Fritzing 0.9.3b)
breadboards: 1

parts:
  Part1 = Arduino Uno (Rev3)
  NEOPIXEL1 = Neopixel_Strip_Black_30_m
  R1 = Trimmer Potentiometer [maximum_resistance=50kΩ package=THT]

nets:
  N1: Part1.A2, R1.wiper
  N2: Part1.D6_PWM, NEOPIXEL1.connector2
  N3: Part1.5V, NEOPIXEL1.connector3, R1.leg2
  N4: Part1.GND, NEOPIXEL1.connector1, R1.leg1
